// Logisim project code_workbench.circ as structural Verilog: 11 circuits, main circuit main
module main (
  input  Switch,
  input  A0,
  input  A1,
  input  A2,
  input  A3,
  input  A4,
  input  A5,
  input  A6,
  input  A7,
  input  B0,
  input  B1,
  input  B2,
  input  B3,
  input  B4,
  input  B5,
  input  B6,
  input  B7,
  output Out0,
  output Out1,
  output Out2,
  output Out3,
  output Out4,
  output Out5,
  output Out6,
  output Out7
);

  _2_to_1_selector u_2_to_1_selector_1 (.A(A0), .B(B0), .Switch(Switch), .Output(Out0));
  _2_to_1_selector u_2_to_1_selector_2 (.A(A1), .B(B1), .Switch(Switch), .Output(Out1));
  _2_to_1_selector u_2_to_1_selector_3 (.A(A2), .B(B2), .Switch(Switch), .Output(Out2));
  _2_to_1_selector u_2_to_1_selector_4 (.A(A3), .B(B3), .Switch(Switch), .Output(Out3));
  _2_to_1_selector u_2_to_1_selector_5 (.A(A4), .B(B4), .Switch(Switch), .Output(Out4));
  _2_to_1_selector u_2_to_1_selector_6 (.A(A5), .B(B5), .Switch(Switch), .Output(Out5));
  _2_to_1_selector u_2_to_1_selector_7 (.A(A6), .B(B6), .Switch(Switch), .Output(Out6));
  _2_to_1_selector u_2_to_1_selector_8 (.A(A7), .B(B7), .Switch(Switch), .Output(Out7));
endmodule

module flipflop (
  input  R,
  input  S,
  output Q,
  output Qbar
);

  nor nor_1 (Q, R, Qbar);
  nor nor_2 (Qbar, Q, S);
endmodule

module _8_bit_adder (
  input  Carry_In,
  input  A0,
  input  A1,
  input  A2,
  input  A3,
  input  A4,
  input  A5,
  input  A6,
  input  A7,
  input  B0,
  input  B1,
  input  B2,
  input  B3,
  input  B4,
  input  B5,
  input  B6,
  input  B7,
  output S0,
  output S1,
  output S2,
  output S3,
  output S4,
  output S5,
  output S6,
  output S7,
  output Carry_Out
);

  wire full_adder_1_carry_out, full_adder_2_carry_out, full_adder_3_carry_out, full_adder_4_carry_out,
       full_adder_5_carry_out, full_adder_6_carry_out, full_adder_7_carry_out;

  full_adder full_adder_1 (.Carry_In(Carry_In), .A_In(A0), .B_In(B0), .Sum_Out(S0), .Carry_Out(full_adder_1_carry_out));
  full_adder full_adder_2 (
    .Carry_In(full_adder_1_carry_out), .A_In(A1), .B_In(B1), .Sum_Out(S1), .Carry_Out(full_adder_2_carry_out));
  full_adder full_adder_3 (
    .Carry_In(full_adder_2_carry_out), .A_In(A2), .B_In(B2), .Sum_Out(S2), .Carry_Out(full_adder_3_carry_out));
  full_adder full_adder_4 (
    .Carry_In(full_adder_3_carry_out), .A_In(A3), .B_In(B3), .Sum_Out(S3), .Carry_Out(full_adder_4_carry_out));
  full_adder full_adder_5 (
    .Carry_In(full_adder_4_carry_out), .A_In(A4), .B_In(B4), .Sum_Out(S4), .Carry_Out(full_adder_5_carry_out));
  full_adder full_adder_6 (
    .Carry_In(full_adder_5_carry_out), .A_In(A5), .B_In(B5), .Sum_Out(S5), .Carry_Out(full_adder_6_carry_out));
  full_adder full_adder_7 (
    .Carry_In(full_adder_6_carry_out), .A_In(A6), .B_In(B6), .Sum_Out(S6), .Carry_Out(full_adder_7_carry_out));
  full_adder full_adder_8 (
    .Carry_In(full_adder_7_carry_out), .A_In(A7), .B_In(B7), .Sum_Out(S7), .Carry_Out(Carry_Out));
endmodule

module half_adder (
  input  in_1,
  input  in_2,
  output Sum_out,
  output Carry_out
);

  xor xor_1 (Sum_out, in_1, in_2);
  and and_1 (Carry_out, in_1, in_2);
endmodule

module full_adder (
  input  Carry_In,
  input  A_In,
  input  B_In,
  output Sum_Out,
  output Carry_Out
);

  wire half_adder_1_carry_out, half_adder_1_sum_out, half_adder_2_carry_out;

  half_adder half_adder_1 (
    .in_1(A_In), .in_2(B_In), .Sum_out(half_adder_1_sum_out), .Carry_out(half_adder_1_carry_out));
  half_adder half_adder_2 (
    .in_1(Carry_In), .in_2(half_adder_1_sum_out), .Sum_out(Sum_Out), .Carry_out(half_adder_2_carry_out));
  or or_1 (Carry_Out, half_adder_2_carry_out, half_adder_1_carry_out);
endmodule

module _8_bit_ones_complement (
  input  In0,
  input  In1,
  input  In2,
  input  In3,
  input  In4,
  input  In5,
  input  In6,
  input  In7,
  input  Invert,
  output Out0,
  output Out1,
  output Out2,
  output Out3,
  output Out4,
  output Out5,
  output Out6,
  output Out7
);

  xor xor_1 (Out0, Invert, In0);
  xor xor_2 (Out1, Invert, In1);
  xor xor_3 (Out2, Invert, In2);
  xor xor_4 (Out3, Invert, In3);
  xor xor_5 (Out4, Invert, In4);
  xor xor_6 (Out5, Invert, In5);
  xor xor_7 (Out6, Invert, In6);
  xor xor_8 (Out7, Invert, In7);
endmodule

module _8_bit_adder_subtractor (
  input  SUB,
  input  A0,
  input  A1,
  input  A2,
  input  A3,
  input  A4,
  input  A5,
  input  A6,
  input  A7,
  input  B0,
  input  B1,
  input  B2,
  input  B3,
  input  B4,
  input  B5,
  input  B6,
  input  B7,
  output S0,
  output S1,
  output S2,
  output S3,
  output S4,
  output S5,
  output S6,
  output S7,
  output Overflow_Underflow
);

  wire n8_bit_adder_1_carry_out, n8_bit_ones_complement_1_out0, n8_bit_ones_complement_1_out1,
       n8_bit_ones_complement_1_out2, n8_bit_ones_complement_1_out3, n8_bit_ones_complement_1_out4,
       n8_bit_ones_complement_1_out5, n8_bit_ones_complement_1_out6, n8_bit_ones_complement_1_out7;

  _8_bit_ones_complement u_8_bit_ones_complement_1 (
    .In0(B0), .In1(B1), .In2(B2), .In3(B3), .In4(B4), .In5(B5), .In6(B6), .In7(B7), .Invert(SUB),
    .Out0(n8_bit_ones_complement_1_out0), .Out1(n8_bit_ones_complement_1_out1),
    .Out2(n8_bit_ones_complement_1_out2), .Out3(n8_bit_ones_complement_1_out3),
    .Out4(n8_bit_ones_complement_1_out4), .Out5(n8_bit_ones_complement_1_out5),
    .Out6(n8_bit_ones_complement_1_out6), .Out7(n8_bit_ones_complement_1_out7));
  _8_bit_adder u_8_bit_adder_1 (
    .Carry_In(SUB), .A0(A0), .A1(A1), .A2(A2), .A3(A3), .A4(A4), .A5(A5), .A6(A6), .A7(A7),
    .B0(n8_bit_ones_complement_1_out0), .B1(n8_bit_ones_complement_1_out1),
    .B2(n8_bit_ones_complement_1_out2), .B3(n8_bit_ones_complement_1_out3),
    .B4(n8_bit_ones_complement_1_out4), .B5(n8_bit_ones_complement_1_out5),
    .B6(n8_bit_ones_complement_1_out6), .B7(n8_bit_ones_complement_1_out7), .S0(S0), .S1(S1), .S2(S2),
    .S3(S3), .S4(S4), .S5(S5), .S6(S6), .S7(S7), .Carry_Out(n8_bit_adder_1_carry_out));
  xor xor_1 (Overflow_Underflow, n8_bit_adder_1_carry_out, SUB);
endmodule

module level_triggered_D_type_flip_flop (
  input  clock,
  input  data,
  output Q,
  output Qbar
);

  wire and_1_out, and_2_out, not_1_out;

  not not_1 (not_1_out, data);
  and and_1 (and_1_out, not_1_out, clock);
  and and_2 (and_2_out, clock, data);
  nor nor_1 (Q, and_1_out, Qbar);
  nor nor_2 (Qbar, Q, and_2_out);
endmodule

module _8_bit_latch (
  input  Clk,
  input  D0,
  input  D1,
  input  D2,
  input  D3,
  input  D4,
  input  D5,
  input  D6,
  input  D7,
  output Q0,
  output Q1,
  output Q2,
  output Q3,
  output Q4,
  output Q5,
  output Q6,
  output Q7
);

  level_triggered_D_type_flip_flop level_triggered_d_type_flip_flop_1 (.clock(Clk), .data(D0), .Q(Q0));  // open: Qbar
  level_triggered_D_type_flip_flop level_triggered_d_type_flip_flop_2 (.clock(Clk), .data(D1), .Q(Q1));  // open: Qbar
  level_triggered_D_type_flip_flop level_triggered_d_type_flip_flop_3 (.clock(Clk), .data(D2), .Q(Q2));  // open: Qbar
  level_triggered_D_type_flip_flop level_triggered_d_type_flip_flop_4 (.clock(Clk), .data(D3), .Q(Q3));  // open: Qbar
  level_triggered_D_type_flip_flop level_triggered_d_type_flip_flop_5 (.clock(Clk), .data(D4), .Q(Q4));  // open: Qbar
  level_triggered_D_type_flip_flop level_triggered_d_type_flip_flop_6 (.clock(Clk), .data(D5), .Q(Q5));  // open: Qbar
  level_triggered_D_type_flip_flop level_triggered_d_type_flip_flop_7 (.clock(Clk), .data(D6), .Q(Q6));  // open: Qbar
  level_triggered_D_type_flip_flop level_triggered_d_type_flip_flop_8 (.clock(Clk), .data(D7), .Q(Q7));  // open: Qbar
endmodule

module _2_to_1_selector (
  input  Switch,
  input  A,
  input  B,
  output Output
);

  wire and_1_out, and_2_out, not_1_out;

  not not_1 (not_1_out, Switch);
  and and_1 (and_1_out, A, not_1_out);
  and and_2 (and_2_out, B, Switch);
  or or_1 (Output, and_1_out, and_2_out);
endmodule

module _8_bit_2_to_1_selector_switch (
  input  Switch,
  input  A0,
  input  A1,
  input  A2,
  input  A3,
  input  A4,
  input  A5,
  input  A6,
  input  A7,
  input  B0,
  input  B1,
  input  B2,
  input  B3,
  input  B4,
  input  B5,
  input  B6,
  input  B7,
  output Out0,
  output Out1,
  output Out2,
  output Out3,
  output Out4,
  output Out5,
  output Out6,
  output Out7
);

  _2_to_1_selector u_2_to_1_selector_1 (.A(A0), .B(B0), .Switch(Switch), .Output(Out0));
  _2_to_1_selector u_2_to_1_selector_2 (.A(A1), .B(B1), .Switch(Switch), .Output(Out1));
  _2_to_1_selector u_2_to_1_selector_3 (.A(A2), .B(B2), .Switch(Switch), .Output(Out2));
  _2_to_1_selector u_2_to_1_selector_4 (.A(A3), .B(B3), .Switch(Switch), .Output(Out3));
  _2_to_1_selector u_2_to_1_selector_5 (.A(A4), .B(B4), .Switch(Switch), .Output(Out4));
  _2_to_1_selector u_2_to_1_selector_6 (.A(A5), .B(B5), .Switch(Switch), .Output(Out5));
  _2_to_1_selector u_2_to_1_selector_7 (.A(A6), .B(B6), .Switch(Switch), .Output(Out6));
  _2_to_1_selector u_2_to_1_selector_8 (.A(A7), .B(B7), .Switch(Switch), .Output(Out7));

  // Notes on the sheet:
  //   0 is A, 1 is B
endmodule
