// Logisim project flipflop.circ as structural Verilog: 2 circuits, main circuit main
module main (
  input  R,
  input  S,
  output out_3
);

  wire nor_1_out, nor_2_out;

  flipflop flipflop_1 ();  // open: R, S, Q, Qbar
  nor nor_1 (nor_1_out, R, nor_2_out);
  nor nor_2 (nor_2_out, nor_1_out, S);
  flipflop flipflop_2 ();  // open: R, S, Q, Qbar
  // Probe on nor_1_out
  // Probe on nor_2_out
endmodule

module flipflop (
  input  R,
  input  S,
  output Q,
  output Qbar
);

  nor nor_1 (Q, R, Qbar);
  nor nor_2 (Qbar, Q, S);
endmodule
